// Digital circuit ALU.dig as structural Verilog
module ALU (
  input  [7:0] A,
  input  [7:0] B,
  input  [2:0] Do_Math,
  output [7:0] Res,
  output C_F,
  output O_F,
  output N_F,
  output Z_F
);

  wire _8bits_adder_2_c_o;
  wire [7:0] _8bits_adder_2_s, _8bits_adder_3_s, ADD_O, AND_O, demultiplexer_1_out_0, demultiplexer_1_out_1,
       MUL_O, not_1_out, not_4_out, NOT_O, OR_O, SUB_O, XOR_O;

  Multiplexer #(.Selector_Bits(3), .Bits(8)) multiplexer_1 (
    .sel(Do_Math), .in_0(ADD_O), .in_1(SUB_O), .in_2(MUL_O), .in_3({8{1'b0}}), .in_4(AND_O), .in_5(OR_O),
    .in_6(XOR_O), .in_7(NOT_O), .out(Res));
  nor nor_1 (Z_F, Res[0], Res[1], Res[2], Res[3], Res[4], Res[5], Res[6], Res[7]);
  assign not_1_out = ~B;  // Not not_1, 8 bits wide
  _8bits_multiplier _8bits_multiplier_1 (.A(A), .B(B), .M(MUL_O), .O_F(O_F));
  assign AND_O = A & B;  // And and_1, 8 bits wide
  assign OR_O = A | B;  // Or or_1, 8 bits wide
  assign XOR_O = A ^ B;  // XOr xor_1, 8 bits wide
  assign NOT_O = ~A;  // Not not_2, 8 bits wide
  _8bits_adder _8bits_adder_1 (.A(A), .B(B), .C(1'b0), .S(ADD_O), .C_o(C_F));
  _8bits_adder _8bits_adder_2 (.A(A), .B(not_1_out), .C(1'b0), .S(_8bits_adder_2_s), .C_o(_8bits_adder_2_c_o));
  not not_3 (N_F, _8bits_adder_2_c_o);
  Demultiplexer #(.Bits(8)) demultiplexer_1 (
    .sel(_8bits_adder_2_c_o), .in(_8bits_adder_2_s), .out_0(demultiplexer_1_out_0),
    .out_1(demultiplexer_1_out_1));
  assign not_4_out = ~demultiplexer_1_out_0;  // Not not_4, 8 bits wide
  _8bits_adder _8bits_adder_3 (
    .A({8{1'b0}}), .B(demultiplexer_1_out_1), .C(_8bits_adder_2_c_o), .S(_8bits_adder_3_s));  // open: C_o
  Multiplexer #(.Bits(8)) multiplexer_2 (
    .sel(_8bits_adder_2_c_o), .in_0(not_4_out), .in_1(_8bits_adder_3_s), .out(SUB_O));

  // Other names for the same wires on the sheet: C_O = C_F

  // Notes on the sheet:
  //   A: default 4
  //   B: default 100
  //   Do_Math: default 2
  //   000 ADD
  //   001 SUB
  //   010 MUL
  //   011 DIV (NOT IMPLEMENTED)
  //   100 AND
  //   101 OR
  //   110 XOR
  //   111 NOT
endmodule

/* Test case:
A	B	Do_{Math}	O_{F}	N_{F}	Z{F}	Result
2	5	1		0		0	0		0	0
2	5	1		0		1	0		3	1
250	15	0		0		0	0		0	0
250	15	0		1		0	0		9	1
50	50	1		0		0	0		0	0
50	50	1		0		0	1		0	1
0	0	0		0		0	0		0	0
0	0	0		0		0	1		0	1
255	1	0		0		0	0		0	0
255	1	0		1		0	1		0	1
4	100	2		0		0	0		0	0
4	100	2		0		0	0		0	1
4	100	2		0		0	0		0	0
4	100	2		1		0	0		0	1
4	100	2		1		0	0		0	0
4	100	2		0		0	0		0	1
2	3	2		0		0	0		0	0
2	3	2		0		0	0		0	1
2	3	2		0		0	0		0	0
2	3	2		0		0	0		6	1
*/
